# Fritzing sketch flashing light (saved by Fritzing 0.9.4)
breadboards: 1

parts:
  Part1 = Arduino Uno (Rev3)
  LED1 = LED - 5mm [color="Green (560nm)" package="5 mm [THT]"]
  R1 = Resistor [tolerance=±5% resistance=180 package=THT]

nets:
  N1: Part1.D13/SCK, LED1.anode
  N2: Part1.GND, R1.Pin_0
  N3: LED1.cathode, R1.Pin_1
